# Fritzing sketch MH-Z19C Wiring (saved by Fritzing 1.0.4)
breadboards: 1

parts:
  A1 = Arduino UNO R4 WiFi
  Mod1 = KY-019 5V Relay Module [package="Breakout board"]
  F1 = Fan - Ventilador [package=THT]
  TD-er1 = MH-Z19 CO2 sensor [part_number=MH-Z19]
  VCC1 = 4 x AA Battery Box
  Part1 = LCD1602-I2C
  J1 = Camdenboss CTB0158-2 [part_number=CTB0158-2 package=THT]

nets:
  VIN: A1.Pin_8, A1.Pin_27, Mod1.+, TD-er1.Vin, Part1.VCC
  GND: A1.Pin_9, A1.Pin_25, A1.Pin_48, Mod1.-, TD-er1.GND, Part1.GND
  N1: A1.Pin_16, Part1.SDA
  N2: A1.Pin_17, Part1.SCL
  N3: A1.Pin_36, TD-er1.TX
  N4: A1.Pin_37, TD-er1.RX
  N5: A1.Pin_38, Mod1.S
  N6: Mod1.Common, F1.5V
  N7: Mod1.NO, VCC1.+, J1.pin1
  N8: F1.GND, VCC1.-, J1.pin2

custom parts:
  Arduino UNO R4 WiFi: The Arduino UNO R4 WiFi merges the RA4M1 microprocessor from Renesas with the ESP32-S3 from Espressif, creating an all-in-one tool for makers with enhanced processing power and a diverse array of new peripherals.
  KY-019 5V Relay Module: KY-019 5V Relay module, used to control AC circuits. (Special thanks to vanepp for fixing the PCB holes and other errors)
  Fan - Ventilador: Ventilador de 2 pines, se encuentra comunmente en computadoras de escritorio
  4 x AA Battery Box: A 4 x AA battery box.
  LCD1602-I2C: A standard character display, usually with 2x16 characters. Comes in many colors with LCM1602 IIC attached.
